# Fritzing sketch Circuit Diagram (saved by Fritzing 0.9.3b)

parts:
  U2 = LM2596 step down module
  esp1 = ESP32 DevKitc V4
  OBD2 = SN65HVD230 CAN Bus transciever module [package=THT]
  U3 = OBDII [package=obdii]
  KeyFob = IC, SIP package, 6 pins [chip_label=KeyFob]

nets:
  N1: U2.IN+, U3.BATTPOWER
  N2: U2.IN-, U2.OUT-, esp1.GND, OBD2.pin_2, U3.CHASGND, U3.SIGGND
  N3: U2.OUT+, esp1.3V3, OBD2.pin_1
  N4: esp1.IO21, OBD2.pin_4
  N5: esp1.IO22, OBD2.pin_3
  N6: esp1.IO32, KeyFob.pin1
  N7: esp1.IO33, KeyFob.pin2
  N8: esp1.IO25, KeyFob.pin3
  N9: esp1.IO27, KeyFob.pin6
  N10: esp1.IO12, KeyFob.pin4
  N11: OBD2.pin_5, U3.CANHIGH
  N12: OBD2.pin_6, U3.ISOL-LINE

notes:
  Lock
  unLock
  Trunk
  Start/Stop
  Vcc
  GND

custom parts:
  LM2596 step down module: LM2596 DC-DC step down power supply module 3 A.
  ESP32 DevKitc V4: ESP32-DevKitC board with ESP32-WROOM-32 module. ESP32-DevKitC V4 is a small-sized ESP32-based development board produced by Espressif. Most of the pins on the ESP module are broken out to the pin headers on the board. The pins D0, D1, D2, D3, CMD and CLK are used internally for communication between ESP32 and SPI flash memory. They are grouped on both sides near the USB connector. Avoid using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
  SN65HVD230 CAN Bus transciever module: Bus Transceiver SN65HVD230 CAN Communication Module, for Arduino.

// code stored in the sketch: Untitled2.ino

